// Logisim project CPU.circ as structural Verilog: 2 circuits, main circuit ULA
module ULA (
  input  [15:0] A,
  input  [15:0] B,
  input  [3:0] op,
  output [15:0] out_4,
  output out_5
);

  wire OutBg, OutEq;
  wire [15:0] OutDiv, OutE, OutNot, OutOr, OutSub, OutSum, OutTimes;

  assign OutE = A & B;  // AND_Gate and_1, 16 bits wide
  assign OutOr = A | B;  // OR_Gate or_1, 16 bits wide
  assign OutNot = ~A;  // NOT_Gate not_1, 16 bits wide
  Adder #(.width(16)) adder_1 (.a(A), .b(B), .out(OutSum));  // open: cin, cout
  Multiplier #(.width(16)) multiplier_1 (.a(A), .b(B), .out(OutTimes));  // open: cin, cout
  Subtractor #(.width(16)) subtractor_1 (.a(A), .b(B), .out(OutSub));  // open: bin, bout
  Divider #(.width(16)) divider_1 (.a(A), .b(B), .out(OutDiv));  // open: upper, rem
  Comparator #(.width(16)) comparator_1 (.a(A), .b(B), .gt(OutBg), .eq(OutEq));  // open: lt
  Multiplexer #(.select(4), .width(16), .enable("false")) multiplexer_1 (
    .in0(OutSum), .in1(OutTimes), .in2(OutSub), .in3(OutDiv), .in4(OutE), .in5(OutOr), .in6(OutNot),
    .in14({16{1'b0}}), .in15({16{1'b0}}), .out(out_4), .sel(op));  // open: in7, in8, in9, in10, in11, in12, in13
  Multiplexer #(.select(4), .enable("false")) multiplexer_2 (
    .in14(OutBg), .in15(OutEq), .out(out_5), .sel(op));  // open: in0, in1, in2, in3, in4, in5, in6, in7, in8, in9, in10, in11, in12, in13
endmodule

module Main (
  input  [15:0] in_1,
  input  [15:0] in_2,
  input  [3:0] in_3,
  output [15:0] out_4
);

  ULA ula_1 (.A(in_1), .B(in_2), .op(in_3), .out_4(out_4));  // open: out_5
endmodule
